// Logisim project new_CPU.circ as structural Verilog: 5 circuits, main circuit main
module main (
  output [3:0] out_1,
  output [3:0] out_2,
  output [3:0] out_3,
  output [3:0] out_4,
  output [3:0] out_5,
  output [3:0] out_6
);

  wire Adress, ALU, ALUCarry, ALULogic, and_1_out, and_2_out, Clock, demultiplexer_1_out1, Digit, DoJump,
       FlagWrite, Jump, not_1_out, not_2_out, not_3_out, or_1_out, rClkMv, w, Write;
  wire [1:0] myalu_1_aeqb, register_1_q;
  wire [3:0] ALUop, multiplexer_1_out, multiplexer_2_out, multiplexer_3_out, Operation, Outp, r0, r1, r2, r3,
       r4, r5, r6, r7, RAMDigit, rCnt;

  Multiplexer #(.width(4)) multiplexer_1 (.in0(rCnt), .out(multiplexer_1_out), .sel(out_4[0]));  // open: in1
  Multiplexer #(.width(4)) multiplexer_2 (.in0(out_1), .in1(multiplexer_1_out), .out(multiplexer_2_out), .sel(rClkMv));
  TTY #(.cols(33), .rows(5)) tty_1 (.data({r1[2:0], r2}), .clk(r1[3]), .we(1'b1));  // open: clr
  and and_1 (and_1_out, Digit, Adress);
  Registers registers_1 (
    .Data(multiplexer_2_out), .w(w), .t(out_3), .r0(r0), .r1(r1), .r2(r2), .r3(r3), .r4(r4), .r5(r5),
    .r6(r6), .r7(r7), .A(out_3), .B(out_4));
  Demultiplexer #(.disabled("Z")) demultiplexer_1 (.out0(w), .out1(demultiplexer_1_out1), .in(Write), .sel(and_1_out));
  Multiplexer #(.disabled("Z"), .width(4)) multiplexer_3 (
    .in0(out_3), .in1(out_4), .out(multiplexer_3_out), .sel(not_1_out));
  not not_1 (not_1_out, Digit);
  RAM #(.addrWidth(4), .dataWidth(4)) ram_1 (
    .addr(multiplexer_3_out), .we(demultiplexer_1_out1), .oe(1'b1), .clk(demultiplexer_1_out1), .din(out_1),
    .dout(RAMDigit));
  MyALU myalu_1 (
    .Cin(ALUCarry), .Operation(ALUop), .A(out_3), .B(out_4), .M(ALULogic), .Outp(Outp),
    .AeqB(myalu_1_aeqb[0]), .Sign(myalu_1_aeqb[1]));
  Register #(.width(2)) register_1 (.D(myalu_1_aeqb), .clk(and_2_out), .Q(register_1_q));  // open: en, clr
  and and_2 (and_2_out, FlagWrite, not_2_out);
  not not_2 (not_2_out, Clock);
  Clock clock_1 (.out(Clock));
  OperationDecoder operationdecoder_1 (
    .Operation(Operation), .Digit(Digit), .Jump(Jump), .ALULogic(ALULogic), .ALU(ALU), .ALUCarry(ALUCarry),
    .FlagWrite(FlagWrite), .Adress(Adress), .ALUop(ALUop));
  nor nor_1 (Write, Clock, Jump);
  or or_1 (or_1_out, register_1_q[1], register_1_q[0]);
  not not_3 (not_3_out, register_1_q[0]);
  Multiplexer #(.disabled("Z"), .select(2)) multiplexer_4 (
    .in0(register_1_q[0]), .in1(register_1_q[1]), .in2(or_1_out), .in3(not_3_out), .out(DoJump),
    .sel(ALUop[1:0]));
  PC pc_1 (.Clock(Clock), .Operation(Operation), .A_in(out_3), .B_in(out_4));  // open: ClockWait, CA

  assign out_5 = out_3;
  assign out_6 = out_4;

  // Other names for the same wires on the sheet: A[3:0] = out_3; A_in[3:0] = out_3; B[3:0] = out_4; B_in[3:0] = out_4;
  //   Data[3:0] = out_1; ID[3:0] = out_2; ROut[7:0] = {r1, r2}
endmodule

module MyALU (
  input  Cin,
  input  [3:0] Operation,
  input  [3:0] A,
  input  [3:0] B,
  input  M,
  output [3:0] Outp,
  output AeqB,
  output Sign
);

  wire n74181_1_p13, n74181_1_p14, n74181_1_p16, n74181_1_p18, not_2_out;

  // _74181 74181_1: pin names not known; wires that end beside it: B[0], A[1], A[0], B[1], Operation[3], A[2], Operation[2], B[2], Operation[1], A[3], Operation[0], B[3], n74181_1_p13, n74181_1_p14, M, n74181_1_p16, Outp[0], n74181_1_p18, Outp[1], AeqB, Outp[2], Outp[3]
  and and_1 (Sign, n74181_1_p14, not_2_out);
  not not_1 (n74181_1_p13, Cin);
  not not_2 (not_2_out, AeqB);

  // Notes on the sheet:
  //   Cout
  //   Pn
endmodule

module Registers (
  input  [3:0] Data,
  input  w,
  input  [3:0] t,
  output [3:0] r0,
  output [3:0] r1,
  output [3:0] r2,
  output [3:0] r3,
  output [3:0] r4,
  output [3:0] r5,
  output [3:0] r6,
  output [3:0] r7,
  output [3:0] A,
  output [3:0] B
);

  wire r0_w, r1_w, r2_w, r3_w, r4_w, r5_w, r6_w, r7_w;
  wire [2:0] A_t, B_t;

  Register #(.width(4)) register_1 (.D(Data), .clk(r0_w), .Q(r0));  // open: en, clr
  Register #(.width(4)) register_2 (.D(Data), .clk(r1_w), .Q(r1));  // open: en, clr
  Register #(.width(4)) register_3 (.D(Data), .clk(r2_w), .Q(r2));  // open: en, clr
  Register #(.width(4)) register_4 (.D(Data), .clk(r3_w), .Q(r3));  // open: en, clr
  Register #(.width(4)) register_5 (.D(Data), .clk(r4_w), .Q(r4));  // open: en, clr
  Register #(.width(4)) register_6 (.D(Data), .clk(r5_w), .Q(r5));  // open: en, clr
  Register #(.width(4)) register_7 (.D(Data), .clk(r6_w), .Q(r6));  // open: en, clr
  Register #(.width(4)) register_8 (.D(Data), .clk(r7_w), .Q(r7));  // open: en, clr
  Demultiplexer #(.select(3)) demultiplexer_1 (
    .out0(r0_w), .out1(r1_w), .out2(r2_w), .out3(r3_w), .out4(r4_w), .out5(r5_w), .out6(r6_w), .out7(r7_w),
    .in(w), .sel(t[2:0]));
  Multiplexer #(.select(3), .width(4)) multiplexer_1 (
    .in0(r0), .in1(r1), .in2(r2), .in3(r3), .in4(r4), .in5(r5), .in6(r6), .in7(r7), .out(A), .sel(A_t));
  Multiplexer #(.select(3), .width(4)) multiplexer_2 (
    .in0(r0), .in1(r1), .in2(r2), .in3(r3), .in4(r4), .in5(r5), .in6(r6), .in7(r7), .out(B), .sel(B_t));
endmodule

module PC (
  input  Clock,
  input  ClockWait,
  output [7:0] CA,
  output [3:0] Operation,
  output [3:0] A_in,
  output [3:0] B_in
);

  wire ClockUpd, not_1_out;
  wire [7:0] controlled_buffer_1_out, counter_1_q;

  Counter #(.ongoal("stay")) counter_1 (.clk(ClockUpd), .D(CA), .Q(counter_1_q));  // open: clr, load, up, count, carry
  assign controlled_buffer_1_out = not_1_out ? counter_1_q : 8'bz;  // Controlled_Buffer controlled_buffer_1
  ROM #(.dataWidth(12)) rom_1 (.addr(controlled_buffer_1_out), .data({B_in, A_in, Operation}));
  not not_1 (not_1_out, ClockWait);
  and and_1 (ClockUpd, not_1_out, Clock);

  // Other names for the same wires on the sheet: CurrAdress[7:0] = CA

  // Notes on the sheet:
  //   contents of rom_1 (hex, n*v repeats v):
  //   0 128 11c 110 125 11c 110 12c 11c 110 12c 11c 110 12f 11c 110 120 11a 110 127 11d 110 12f 11c 110
  //   122 11d 110 12c 11c 110 124 11c 110
endmodule

module OperationDecoder (
  input  [3:0] Operation,
  output Digit,
  output Jump,
  output ALULogic,
  output ALU,
  output ALUCarry,
  output FlagWrite,
  output Adress,
  output [3:0] ALUop
);

  wire [15:7] rom_1_data;

  ROM #(.addrWidth(4), .dataWidth(16)) rom_1 (
    .addr(Operation), .data({rom_1_data, Adress, FlagWrite, ALUCarry, ALU, ALULogic, Jump, Digit}));

  assign ALUop = Operation;

  // Notes on the sheet:
  //   contents of rom_1 (hex, n*v repeats v):
  //   0 1 41 40 c 0 38 0 0 8 0 0 4*2
endmodule
