// Logisim project main.circ as structural Verilog: 12 circuits, main circuit main
module main (
);

  wire clock_1_out, clock_2_out, cpu_1_mr, cpu_1_mw, cpu_1_nothalt, dipswitch_1_sw1, dipswitch_1_sw2;
  wire [7:0] cpu_1_dataout, ram_1_dout;
  wire [15:0] cpu_1_address;

  Clock #(.highDuration(2), .lowDuration(2)) clock_1 (.out(clock_1_out));
  DipSwitch #(.number(2)) dipswitch_1 (.sw1(dipswitch_1_sw1), .sw2(dipswitch_1_sw2));
  Clock clock_2 (.out(clock_2_out));
  CPU cpu_1 (
    .DataIn(ram_1_dout), .Clk(clock_1_out), .NotReset(dipswitch_1_sw1), .NotWait(dipswitch_1_sw2),
    .DataOut(cpu_1_dataout), .NotHalt(cpu_1_nothalt), .MR(cpu_1_mr), .MW(cpu_1_mw), .Address(cpu_1_address));
  LED led_1 (.in(cpu_1_nothalt));
  RAM #(.addrWidth(16)) ram_1 (
    .addr(cpu_1_address), .we(cpu_1_mw), .oe(cpu_1_mr), .clk(clock_2_out), .din(cpu_1_dataout),
    .dout(ram_1_dout));
endmodule

module StackPointer (
  input  DHWrite,
  input  NotReset,
  input  [7:0] DIn,
  input  DLWrite,
  input  DHRead,
  input  ARead,
  input  NotDec,
  input  NotInc,
  input  Clk,
  input  DLRead,
  output [15:0] AOut,
  output [7:0] DOut
);

  wire n74193_1_pin4, n74193_1_pin5, n74193_1_pin11, n74193_2_pin4, n74193_2_pin5, n74193_3_pin4,
       n74193_3_pin5, n74193_3_pin11, n74193_4_pin4, n74193_4_pin5, not_1_out;
  wire [3:0] n74193_1_pin3, n74193_2_pin3;
  wire [7:0] n74193_4_pin3;

  not not_1 (not_1_out, NotReset);
  _74193 u_74193_1 (
    .pin1(DIn[5]), .pin2(n74193_1_pin3[1]), .pin3(n74193_1_pin3[0]), .pin4(n74193_1_pin4),
    .pin5(n74193_1_pin5), .pin6(n74193_1_pin3[2]), .pin7(n74193_1_pin3[3]), .pin15(DIn[4]),
    .pin14(not_1_out), .pin11(n74193_1_pin11), .pin10(DIn[6]), .pin9(DIn[7]));  // open: pin13, pin12
  assign DOut = DHRead ? {n74193_1_pin3, n74193_2_pin3} : 8'bz;  // Controlled_Buffer controlled_buffer_1
  _74193 u_74193_2 (
    .pin1(DIn[1]), .pin2(n74193_2_pin3[1]), .pin3(n74193_2_pin3[0]), .pin4(n74193_2_pin4),
    .pin5(n74193_2_pin5), .pin6(n74193_2_pin3[2]), .pin7(n74193_2_pin3[3]), .pin15(DIn[0]),
    .pin14(not_1_out), .pin13(n74193_1_pin4), .pin12(n74193_1_pin5), .pin11(n74193_1_pin11), .pin10(DIn[2]),
    .pin9(DIn[3]));
  assign AOut = ARead ? {n74193_1_pin3, n74193_2_pin3, n74193_4_pin3} : 16'bz;  // Controlled_Buffer controlled_buffer_2
  _74193 u_74193_3 (
    .pin1(DIn[5]), .pin2(n74193_4_pin3[5]), .pin3(n74193_4_pin3[4]), .pin4(n74193_3_pin4),
    .pin5(n74193_3_pin5), .pin6(n74193_4_pin3[6]), .pin7(n74193_4_pin3[7]), .pin15(DIn[4]),
    .pin14(not_1_out), .pin13(n74193_2_pin4), .pin12(n74193_2_pin5), .pin11(n74193_3_pin11), .pin10(DIn[6]),
    .pin9(DIn[7]));
  Hex_Digit_Display hex_digit_display_1 (.value(n74193_1_pin3));  // open: dp
  _74193 u_74193_4 (
    .pin1(DIn[1]), .pin2(n74193_4_pin3[1]), .pin3(n74193_4_pin3[0]), .pin4(n74193_4_pin4),
    .pin5(n74193_4_pin5), .pin6(n74193_4_pin3[2]), .pin7(n74193_4_pin3[3]), .pin15(DIn[0]),
    .pin14(not_1_out), .pin13(n74193_3_pin4), .pin12(n74193_3_pin5), .pin11(n74193_3_pin11), .pin10(DIn[2]),
    .pin9(DIn[3]));
  assign DOut = DLRead ? n74193_4_pin3 : 8'bz;  // Controlled_Buffer controlled_buffer_3
  Hex_Digit_Display hex_digit_display_2 (.value(n74193_2_pin3));  // open: dp
  Hex_Digit_Display hex_digit_display_3 (.value(n74193_4_pin3[7:4]));  // open: dp
  Hex_Digit_Display hex_digit_display_4 (.value(n74193_4_pin3[3:0]));  // open: dp
  nand nand_1 (n74193_1_pin11, DHWrite, Clk);
  nand nand_2 (n74193_3_pin11, DLWrite, Clk);
  or or_1 (n74193_4_pin4, NotDec, Clk);
  or or_2 (n74193_4_pin5, NotInc, Clk);
endmodule

module CPU (
  input  [7:0] DataIn,
  input  Clk,
  input  NotReset,
  input  NotWait,
  output [7:0] DataOut,
  output NotHalt,
  output MR,
  output MW,
  output [15:0] Address
);

  wire ADIn, ADOut, ALUC, ALUEn, ALUM, FRALUIn, FRDIn, FRDOut, IRDIn, NotPCInc, NotSPDec, NotSPInc, or_1_out,
       PCARead, PCDHRead, PCDHWrite, PCDLRead, PCDLWrite, SCClear, SPARead, SPDHRead, SPDHWrite, SPDLRead,
       SPDLWrite, TARead, TDHWrite, TDLRead, TDLWrite;
  wire [2:0] alu_1_flagsout, Flags, RFIdxIn, RFIdxOut;
  wire [3:0] ALUOp, Step;
  wire [7:0] Accum, DBus, Instruction, temporaryregister_1_hout;
  wire [15:0] ABus;

  LedBar #(.matrixcols(3)) ledbar_1 (.led0(Flags[0]), .led1(Flags[1]), .led2(Flags[2]));
  Hex_Digit_Display hex_digit_display_1 (.value(Step));  // open: dp
  Hex_Digit_Display hex_digit_display_2 (.value(Accum[7:4]));  // open: dp
  Hex_Digit_Display hex_digit_display_3 (.value(Accum[3:0]));  // open: dp
  Hex_Digit_Display hex_digit_display_4 (.value(Instruction[7:4]));  // open: dp
  StackPointer stackpointer_1 (
    .DHWrite(SPDHWrite), .NotReset(NotReset), .DIn(DBus), .DLWrite(SPDLWrite), .DHRead(SPDHRead),
    .ARead(SPARead), .NotDec(NotSPDec), .NotInc(NotSPInc), .Clk(Clk), .DLRead(SPDLRead), .AOut(ABus),
    .DOut(DBus));
  Hex_Digit_Display hex_digit_display_5 (.value(Instruction[3:0]));  // open: dp
  Hex_Digit_Display hex_digit_display_6 (.value(DBus[7:4]));  // open: dp
  Hex_Digit_Display hex_digit_display_7 (.value(DBus[3:0]));  // open: dp
  RegisterFile registerfile_1 (
    .DIn(DBus), .WriteId(RFIdxIn), .ReadId(RFIdxOut), .NotReset(NotReset), .Clk(Clk), .DOut(DBus));
  Hex_Digit_Display hex_digit_display_8 (.value(ABus[15:12]));  // open: dp
  Hex_Digit_Display hex_digit_display_9 (.value(ABus[11:8]));  // open: dp
  Hex_Digit_Display hex_digit_display_10 (.value(ABus[7:4]));  // open: dp
  ProgramCounter programcounter_1 (
    .NotReset(NotReset), .DHWrite(PCDHWrite), .Clk(Clk), .DHRead(PCDHRead), .DIn(DBus), .ARead(PCARead),
    .DLWrite(PCDLWrite), .NotInc(NotPCInc), .DLRead(PCDLRead), .DOut(DBus), .AOut(ABus));
  Hex_Digit_Display hex_digit_display_11 (.value(ABus[3:0]));  // open: dp
  InstructionRegister instructionregister_1 (
    .DIn(DBus), .Write(IRDIn), .Clk(Clk), .NotReset(NotReset), .Instruction(Instruction));
  Accumulator accumulator_1 (
    .Read(ADOut), .DIn(DBus), .Write(ADIn), .Clk(Clk), .NotReset(NotReset), .DOut(DBus), .ALUOut(Accum));
  TemporaryRegister temporaryregister_1 (
    .ARead(TARead), .DLRead(TDLRead), .NotReset(NotReset), .DHWrite(TDHWrite), .Clk(Clk), .DIn(DBus),
    .DLWrite(TDLWrite), .AOut(ABus), .DOut(DBus), .HOut(temporaryregister_1_hout));
  ALU alu_1 (
    .AccumulatorIn(Accum), .Enable(ALUEn), .DIn(temporaryregister_1_hout), .Opcode(ALUOp), .Carry(ALUC),
    .Mode(ALUM), .DOut(DBus), .FlagsOut(alu_1_flagsout));
  assign Address = or_1_out ? ABus : 16'bz;  // Controlled_Buffer controlled_buffer_1
  or or_1 (or_1_out, MR, MW);
  assign DBus = MR ? DataIn : 8'bz;  // Controlled_Buffer controlled_buffer_2
  assign DataOut = MW ? DBus : 8'bz;  // Controlled_Buffer controlled_buffer_3
  FlagRegister flagregister_1 (
    .FlagsIn(alu_1_flagsout), .DIn(DBus), .Write(FRDIn), .ALUWrite(FRALUIn), .Read(FRDOut), .Clk(Clk),
    .NotReset(NotReset), .FlagsOut(Flags), .DOut(DBus));
  StepCounter stepcounter_1 (
    .Clk(Clk), .NotReset(NotReset), .Clear(SCClear), .NotHalt(NotHalt), .NotWait(NotWait), .Step(Step));
  InstructionDecoder instructiondecoder_1 (
    .Instruction(Instruction), .Flags(Flags), .Step(Step), .MemoryRead(MR), .MemoryWrite(MW),
    .FRALUIn(FRALUIn), .FRDOut(FRDOut), .FRDIn(FRDIn), .NotHalt(NotHalt), .ALUEn(ALUEn), .NotALUC(ALUC),
    .ALUM(ALUM), .ADOut(ADOut), .ADIn(ADIn), .SCClear(SCClear), .TARead(TARead), .TDLRead(TDLRead),
    .TDHWrite(TDHWrite), .TDLWrite(TDLWrite), .IRDIn(IRDIn), .PCDHWrite(PCDHWrite), .PCDLWrite(PCDLWrite),
    .PCDHRead(PCDHRead), .PCDLRead(PCDLRead), .NotPCInc(NotPCInc), .PCARead(PCARead), .SPDHWrite(SPDHWrite),
    .SPDLWrite(SPDLWrite), .SPDHRead(SPDHRead), .SPDLRead(SPDLRead), .NotSPInc(NotSPInc), .ALUOp(ALUOp),
    .NotSPDec(NotSPDec), .SPARead(SPARead), .RFIdxIn(RFIdxIn), .RFIdxOut(RFIdxOut));

  // Other names for the same wires on the sheet: MemoryRead = MR; MemoryWrite = MW
endmodule

module TemporaryRegister (
  input  ARead,
  input  DLRead,
  input  NotReset,
  input  DHWrite,
  input  Clk,
  input  [7:0] DIn,
  input  DLWrite,
  output [15:0] AOut,
  output [7:0] DOut,
  output [7:0] HOut
);

  wire n74273_1_pin11, n74273_2_pin11;
  wire [7:0] n74273_2_pin2;

  _74273 u_74273_1 (
    .pin1(NotReset), .pin2(HOut[0]), .pin3(DIn[0]), .pin4(DIn[1]), .pin5(HOut[1]), .pin6(HOut[2]),
    .pin7(DIn[2]), .pin8(DIn[3]), .pin9(HOut[3]), .pin19(HOut[7]), .pin18(DIn[7]), .pin17(DIn[6]),
    .pin16(HOut[6]), .pin15(HOut[5]), .pin14(DIn[5]), .pin13(DIn[4]), .pin12(HOut[4]), .pin11(n74273_1_pin11));
  and and_1 (n74273_1_pin11, DHWrite, Clk);
  assign AOut = ARead ? {HOut, n74273_2_pin2} : 16'bz;  // Controlled_Buffer controlled_buffer_1
  _74273 u_74273_2 (
    .pin1(NotReset), .pin2(n74273_2_pin2[0]), .pin3(DIn[0]), .pin4(DIn[1]), .pin5(n74273_2_pin2[1]),
    .pin6(n74273_2_pin2[2]), .pin7(DIn[2]), .pin8(DIn[3]), .pin9(n74273_2_pin2[3]), .pin19(n74273_2_pin2[7]),
    .pin18(DIn[7]), .pin17(DIn[6]), .pin16(n74273_2_pin2[6]), .pin15(n74273_2_pin2[5]), .pin14(DIn[5]),
    .pin13(DIn[4]), .pin12(n74273_2_pin2[4]), .pin11(n74273_2_pin11));
  and and_2 (n74273_2_pin11, DLWrite, Clk);
  assign DOut = DLRead ? n74273_2_pin2 : 8'bz;  // Controlled_Buffer controlled_buffer_2
endmodule

module Accumulator (
  input  Read,
  input  [7:0] DIn,
  input  Write,
  input  Clk,
  input  NotReset,
  output [7:0] DOut,
  output [7:0] ALUOut
);

  wire not_1_out;

  assign DOut = Read ? ALUOut : 8'bz;  // Controlled_Buffer controlled_buffer_1
  Register register_1 (.D(DIn), .en(Write), .clk(Clk), .Q(ALUOut), .clr(not_1_out));
  not not_1 (not_1_out, NotReset);
endmodule

module ALU (
  input  [7:0] AccumulatorIn,
  input  Enable,
  input  [7:0] DIn,
  input  [3:0] Opcode,
  input  Carry,
  input  Mode,
  output [7:0] DOut,
  output [2:0] FlagsOut
);

  wire n74181_1_p13, NotCarry, Sign, Zero;
  wire [6:0] n74181_2_p17;

  // _74181 74181_1: pin names not known; wires that end beside it: DIn[4], AccumulatorIn[5], AccumulatorIn[4], DIn[5], Opcode[3], AccumulatorIn[6], Opcode[2], DIn[6], Opcode[1], AccumulatorIn[7], Opcode[0], DIn[7], n74181_1_p13, Mode, NotCarry, n74181_2_p17[4], n74181_2_p17[5], Sign
  // _74181 74181_2: pin names not known; wires that end beside it: n74181_2_p17[6], DIn[0], AccumulatorIn[1], AccumulatorIn[0], DIn[1], Opcode[3], AccumulatorIn[2], Opcode[2], DIn[2], Opcode[1], AccumulatorIn[3], Opcode[0], DIn[3], Carry, Mode, n74181_1_p13, n74181_2_p17[0], n74181_2_p17[1], n74181_2_p17[2], n74181_2_p17[3]
  nor nor_1 (Zero, Sign, n74181_2_p17[6], n74181_2_p17[5], n74181_2_p17[4], n74181_2_p17[2], n74181_2_p17[0], n74181_2_p17[1], n74181_2_p17[3]);
  assign DOut = Enable ? {Sign, n74181_2_p17} : 8'bz;  // Controlled_Buffer controlled_buffer_1
  assign FlagsOut = Enable ? {Zero, NotCarry, Sign} : 3'bz;  // Controlled_Buffer controlled_buffer_2
endmodule

module FlagRegister (
  input  [2:0] FlagsIn,
  input  [7:0] DIn,
  input  Write,
  input  ALUWrite,
  input  Read,
  input  Clk,
  input  NotReset,
  output [2:0] FlagsOut,
  output [7:0] DOut
);

  wire not_1_out, or_1_out;
  wire [4:0] controlled_buffer_1_out, register_1_q;

  assign {controlled_buffer_1_out, FlagsIn} = Write ? DIn : 8'bz;  // Controlled_Buffer controlled_buffer_1
  or or_1 (or_1_out, Write, ALUWrite);
  Register register_1 (
    .D({controlled_buffer_1_out, FlagsIn}), .en(or_1_out), .clk(Clk), .Q({register_1_q, FlagsOut}),
    .clr(not_1_out));
  not not_1 (not_1_out, NotReset);
  assign DOut = Read ? {register_1_q, FlagsOut} : 8'bz;  // Controlled_Buffer controlled_buffer_2
endmodule

module InstructionRegister (
  input  [7:0] DIn,
  input  Write,
  input  Clk,
  input  NotReset,
  output [7:0] Instruction
);

  wire not_1_out;

  Register register_1 (.D(DIn), .en(Write), .clk(Clk), .Q(Instruction), .clr(not_1_out));
  not not_1 (not_1_out, NotReset);
endmodule

module RegisterFile (
  input  [7:0] DIn,
  input  [2:0] WriteId,
  input  [2:0] ReadId,
  input  NotReset,
  input  Clk,
  output [7:0] DOut
);

  wire decoder_1_out0, decoder_1_out1, decoder_1_out2, decoder_1_out3, decoder_1_out4, decoder_1_out5,
       not_1_out;
  wire [7:0] demultiplexer_1_out0, demultiplexer_1_out1, demultiplexer_1_out2, demultiplexer_1_out3,
       demultiplexer_1_out4, demultiplexer_1_out5, register_1_q, register_2_q, register_3_q, register_4_q,
       register_5_q, register_6_q;

  Demultiplexer #(.enable("true"), .select(3), .width(8)) demultiplexer_1 (
    .out0(demultiplexer_1_out0), .out1(demultiplexer_1_out1), .out2(demultiplexer_1_out2),
    .out3(demultiplexer_1_out3), .out4(demultiplexer_1_out4), .out5(demultiplexer_1_out5), .in(DIn),
    .sel(WriteId));  // open: out6, out7, en
  Decoder #(.select(3)) decoder_1 (
    .out0(decoder_1_out0), .out1(decoder_1_out1), .out2(decoder_1_out2), .out3(decoder_1_out3),
    .out4(decoder_1_out4), .out5(decoder_1_out5), .sel(WriteId));  // open: out6, out7, en
  not not_1 (not_1_out, NotReset);
  Register register_1 (.D(demultiplexer_1_out0), .en(decoder_1_out0), .clk(Clk), .Q(register_1_q), .clr(not_1_out));
  Register register_2 (.D(demultiplexer_1_out1), .en(decoder_1_out1), .clk(Clk), .Q(register_2_q), .clr(not_1_out));
  Register register_3 (.D(demultiplexer_1_out2), .en(decoder_1_out2), .clk(Clk), .Q(register_3_q), .clr(not_1_out));
  Register register_4 (.D(demultiplexer_1_out3), .en(decoder_1_out3), .clk(Clk), .Q(register_4_q), .clr(not_1_out));
  Register register_5 (.D(demultiplexer_1_out4), .en(decoder_1_out4), .clk(Clk), .Q(register_5_q), .clr(not_1_out));
  Register register_6 (.D(demultiplexer_1_out5), .en(decoder_1_out5), .clk(Clk), .Q(register_6_q), .clr(not_1_out));
  Multiplexer #(.enable("true"), .select(3), .width(8)) multiplexer_1 (
    .in0(register_1_q), .in1(register_2_q), .in2(register_3_q), .in3(register_4_q), .in4(register_5_q),
    .in5(register_6_q), .out(DOut), .sel(ReadId));  // open: in6, in7, en
endmodule

module InstructionDecoder (
  input  [7:0] Instruction,
  input  [2:0] Flags,
  input  [3:0] Step,
  output MemoryRead,
  output MemoryWrite,
  output FRALUIn,
  output FRDOut,
  output FRDIn,
  output NotHalt,
  output ALUEn,
  output NotALUC,
  output ALUM,
  output ADOut,
  output ADIn,
  output SCClear,
  output TARead,
  output TDLRead,
  output TDHWrite,
  output TDLWrite,
  output IRDIn,
  output PCDHWrite,
  output PCDLWrite,
  output PCDHRead,
  output PCDLRead,
  output NotPCInc,
  output PCARead,
  output SPDHWrite,
  output SPDLWrite,
  output SPDHRead,
  output SPDLRead,
  output NotSPInc,
  output [3:0] ALUOp,
  output NotSPDec,
  output SPARead,
  output [2:0] RFIdxIn,
  output [2:0] RFIdxOut
);

  ROM #(.addrWidth(15)) rom_1 (
    .addr({Step, Flags, Instruction}),
    .data({NotALUC, ALUEn, NotHalt, FRDIn, FRDOut, FRALUIn, MemoryWrite, MemoryRead}));
  ROM #(.addrWidth(15)) rom_2 (
    .addr({Step, Flags, Instruction}),
    .data({TDLWrite, TDHWrite, TDLRead, TARead, SCClear, ADIn, ADOut, ALUM}));
  ROM #(.addrWidth(15)) rom_3 (
    .addr({Step, Flags, Instruction}),
    .data({SPDHWrite, PCARead, NotPCInc, PCDLRead, PCDHRead, PCDLWrite, PCDHWrite, IRDIn}));
  ROM #(.addrWidth(15)) rom_4 (
    .addr({Step, Flags, Instruction}), .data({ALUOp, NotSPInc, SPDLRead, SPDHRead, SPDLWrite}));
  ROM #(.addrWidth(15)) rom_5 (.addr({Step, Flags, Instruction}), .data({RFIdxOut, RFIdxIn, SPARead, NotSPDec}));

  // Notes on the sheet:
  //   contents of rom_1 (hex, n*v repeats v):
  //   17*a1 18*a0 8*a1 25*a0 b0 a8 7*a0 b0 a8 7*a0 b0 a8 7*a0 b0 a8 7*a0 b0 a8 7*a0 b0 a8 9*a0 8*a2 aa a2
  //   a2 a2 7*a1 b1 4*a1 a0 a0 a0 9*a1 a0 a0 a0 a1 a0 a0 a0 5*a1 a0 a0 a0 a2 a1 a1 a2 a2 a1 a2 7*a1 10*a0
  //   a1 7*a0 a1 7*a0 a1 7*a0 a1 7*a0 a1 7*a0 a1 7*a0 a1 80 7*0 17*a1 18*a0 8*a1 25*a0 b0 a8 7*a0 b0 a8
  //   7*a0 b0 a8 7*a0 b0 a8 7*a0 b0 a8 7*a0 b0 a8 9*a0 8*a2 aa a2 a2 a2 7*a1 b1 4*a1 a0 a0 a0 9*a1 a0 a0
  //   a0 5*a1 a0 a0 a0 a1 a0 a0 a0 a2 a1 a1 a2 a1 a2 a2 7*a1 10*a0 a1 7*a0 a1 7*a0 a1 7*a0 a1 7*a0 a1 7*a0
  //   a1 7*a0 a1 80 7*0 17*a1 18*a0 8*a1 25*a0 b0 a8 7*a0 b0 a8 7*a0 b0 a8 7*a0 b0 a8 7*a0 b0 a8 7*a0 b0
  //   a8 9*a0 8*a2 aa a2 a2 a2 7*a1 b1 4*a1 a0 a0 a0 5*a1 a0 a0 a0 5*a1 a0 a0 a0 5*a1 a0 a0 a0 a2 a1 a2 a1
  //   a2 a1 a2 7*a1 10*a0 a1 7*a0 a1 7*a0 a1 7*a0 a1 7*a0 a1 7*a0 a1 7*a0 a1 80 7*0 17*a1 18*a0 8*a1 25*a0
  //   b0 a8 7*a0 b0 a8 7*a0 b0 a8 7*a0 b0 a8 7*a0 b0 a8 7*a0 b0 a8 9*a0 8*a2 aa a2 a2 a2 7*a1 b1 4*a1 a0
  //   a0 a0 5*a1 a0 a0 a0 9*a1 a0 a0 a0 a1 a0 a0 a0 a2 a1 a2 a1 a1 a2 a2 7*a1 10*a0 a1 7*a0 a1 7*a0 a1
  //   7*a0 a1 7*a0 a1 7*a0 a1 7*a0 a1 80 7*0 17*a1 18*a0 8*a1 25*a0 b0 a8 7*a0 b0 a8 7*a0 b0 a8 7*a0 b0 a8
  //   7*a0 b0 a8 7*a0 b0 a8 9*a0 8*a2 aa a2 a2 a2 7*a1 b1 8*a1 a0 a0 a0 5*a1 a0 a0 a0 a1 a0 a0 a0 5*a1 a0
  //   a0 a0 a1 a2 a1 a2 a2 a1 a2 7*a1 10*a0 a1 7*a0 a1 7*a0 a1 7*a0 a1 7*a0 a1 7*a0 a1 7*a0 a1 80 7*0
  //   17*a1 18*a0 8*a1 25*a0 b0 a8 7*a0 b0 a8 7*a0 b0 a8 7*a0 b0 a8 7*a0 b0 a8 7*a0 b0 a8 9*a0 8*a2 aa a2
  //   a2 a2 7*a1 b1 8*a1 a0 a0 a0 5*a1 a0 a0 a0 5*a1 a0 a0 a0 a1 a0 a0 a0 a1 a2 a1 a2 a1 a2 a2 7*a1 10*a0
  //   a1 7*a0 a1 7*a0 a1 7*a0 a1 7*a0 a1 7*a0 a1 7*a0 a1 80 7*0 17*a1 18*a0 8*a1 25*a0 b0 a8 7*a0 b0 a8
  //   7*a0 b0 a8 7*a0 b0 a8 7*a0 b0 a8 7*a0 b0 a8 9*a0 8*a2 aa a2 a2 a2 7*a1 b1 8*a1 a0 a0 a0 a1 a0 a0 a0
  //   5*a1 a0 a0 a0 5*a1 a0 a0 a0 a1 a2 a2 a1 a2 a1 a2 7*a1 10*a0 a1 7*a0 a1 7*a0 a1 7*a0 a1 7*a0 a1 7*a0
  //   a1 7*a0 a1 80 7*0 17*a1 18*a0 8*a1 25*a0 b0 a8 7*a0 b0 a8 7*a0 b0 a8 7*a0 b0 a8 7*a0 b0 a8 7*a0 b0
  //   a8 9*a0 8*a2 aa a2 a2 a2 7*a1 b1 8*a1 a0 a0 a0 a1 a0 a0 a0 9*a1 a0 a0 a0 a1 a0 a0 a0 a1 a2 a2 a1 a1
  //   a2 a2 7*a1 10*a0 a1 7*a0 a1 7*a0 a1 7*a0 a1 7*a0 a1 7*a0 a1 7*a0 a1 80 8*0 16*a1 18*a0 8*a1 18*a0
  //   54*a1 9*a0 7*a1 a2 a1 a2 a2 a2 12*a1 a0 a0 a0 a1 a0 a0 a0 a1 a0 a0 a0 a1 a0 a0 a0 a1 a0 a0 a0 a1 a0
  //   a0 a0 a1 a0 a0 a0 7*a2 7*a1 a0 a0 a0 56*e4 9*0 16*a1 18*a0 8*a1 18*a0 54*a1 9*a0 7*a1 a2 a1 a2 a2 a2
  //   12*a1 a0 a0 a0 a1 a0 a0 a0 a1 a0 a0 a0 a1 a0 a0 a0 a1 a0 a0 a0 a1 a0 a0 a0 a1 a0 a0 a0 7*a2 7*a1 a0
  //   a0 a0 56*e4 9*0 16*a1 18*a0 8*a1 18*a0 54*a1 9*a0 7*a1 a2 a1 a2 a2 a2 12*a1 a0 a0 a0 a1 a0 a0 a0 a1
  //   a0 a0 a0 a1 a0 a0 a0 a1 a0 a0 a0 a1 a0 a0 a0 a1 a0 a0 a0 7*a2 7*a1 a0 a0 a0 56*e4 9*0 16*a1 18*a0
  //   8*a1 18*a0 54*a1 9*a0 7*a1 a2 a1 a2 a2 a2 12*a1 a0 a0 a0 a1 a0 a0 a0 a1 a0 a0 a0 a1 a0 a0 a0 a1 a0
  //   a0 a0 a1 a0 a0 a0 a1 a0 a0 a0 7*a2 7*a1 a0 a0 a0 56*e4 9*0 16*a1 18*a0 8*a1 18*a0 54*a1 9*a0 7*a1 a2
  //   a1 a2 a2 a2 12*a1 a0 a0 a0 a1 a0 a0 a0 a1 a0 a0 a0 a1 a0 a0 a0 a1 a0 a0 a0 a1 a0 a0 a0 a1 a0 a0 a0
  //   7*a2 7*a1 a0 a0 a0 56*e4 9*0 16*a1 18*a0 8*a1 18*a0 54*a1 9*a0 7*a1 a2 a1 a2 a2 a2 12*a1 a0 a0 a0 a1
  //   a0 a0 a0 a1 a0 a0 a0 a1 a0 a0 a0 a1 a0 a0 a0 a1 a0 a0 a0 a1 a0 a0 a0 7*a2 7*a1 a0 a0 a0 56*e4 9*0
  //   16*a1 18*a0 8*a1 18*a0 54*a1 9*a0 7*a1 a2 a1 a2 a2 a2 12*a1 a0 a0 a0 a1 a0 a0 a0 a1 a0 a0 a0 a1 a0
  //   a0 a0 a1 a0 a0 a0 a1 a0 a0 a0 a1 a0 a0 a0 7*a2 7*a1 a0 a0 a0 56*e4 9*0 16*a1 18*a0 8*a1 18*a0 54*a1
  //   9*a0 7*a1 a2 a1 a2 a2 a2 12*a1 a0 a0 a0 a1 a0 a0 a0 a1 a0 a0 a0 a1 a0 a0 a0 a1 a0 a0 a0 a1 a0 a0 a0
  //   a1 a0 a0 a0 7*a2 7*a1 a0 a0 a0 56*e4 16*0 8*a1 b1 5*a1 b1 5*a1 b1 5*a1 b1 7*a2 aa 5*a2 aa 5*a2 aa
  //   5*a2 aa 54*0 9*a1 7*0 a1 0 a1 a1 a1 8*0 a1 a1 a1 a0 4*a1 a0 a0 a0 a1 4*a0 a1 a1 a1 a0 4*a1 4*a0 4*a1
  //   a2 a2 a1 a1 a2 8*a1 a0 a0 a0 56*a1 16*0 8*a1 b1 5*a1 b1 5*a1 b1 5*a1 b1 7*a2 aa 5*a2 aa 5*a2 aa 5*a2
  //   aa 54*0 9*a1 7*0 a1 0 a1 a1 a1 8*0 a1 a1 a1 a0 4*a1 a0 a0 a0 a1 4*a0 4*a1 4*a0 a1 a1 a1 a0 4*a1 a2
  //   a2 a1 a2 9*a1 a0 a0 a0 56*a1 16*0 8*a1 b1 5*a1 b1 5*a1 b1 5*a1 b1 7*a2 aa 5*a2 aa 5*a2 aa 5*a2 aa
  //   54*0 9*a1 7*0 a1 0 a1 a1 a1 8*0 a1 a1 a1 a0 4*a1 4*a0 4*a1 4*a0 4*a1 4*a0 4*a1 a2 a1 a2 a1 a2 8*a1
  //   a0 a0 a0 56*a1 16*0 8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
  //   contents of rom_2 (hex, n*v repeats v):
  //   8 6*0 4 0 52*40 5*0 4 2 7*0 4 2 7*0 4 2 7*0 4 2 7*0 4 2 7*0 4 2 17*0 2 11*0 4 4*0 80 0 0 0 8*8 80 0
  //   0 0 80 0 0 0 4*8 80 4*0 8 8 0 0 8 0 0 8 8 0 0 8 0 80 80 80 6*40 42 7*40 42 7*40 42 7*40 42 7*40 42
  //   7*40 42 7*40 42 40 8*0 8 6*0 4 0 52*40 5*0 4 2 7*0 4 2 7*0 4 2 7*0 4 2 7*0 4 2 7*0 4 2 17*0 2 11*0 4
  //   4*0 80 0 0 0 8*8 80 0 0 0 4*8 80 0 0 0 80 4*0 8 8 0 8 0 0 0 8 8 0 8 0 0 80 80 80 6*40 42 7*40 42
  //   7*40 42 7*40 42 7*40 42 7*40 42 7*40 42 40 8*0 8 6*0 4 0 52*40 5*0 4 2 7*0 4 2 7*0 4 2 7*0 4 2 7*0 4
  //   2 7*0 4 2 17*0 2 11*0 4 4*0 80 0 0 0 4*8 80 0 0 0 4*8 80 0 0 0 4*8 80 4*0 8 0 8 0 8 0 0 8 0 8 0 8 0
  //   80 80 80 6*40 42 7*40 42 7*40 42 7*40 42 7*40 42 7*40 42 7*40 42 40 8*0 8 6*0 4 0 52*40 5*0 4 2 7*0
  //   4 2 7*0 4 2 7*0 4 2 7*0 4 2 7*0 4 2 17*0 2 11*0 4 4*0 80 0 0 0 4*8 80 0 0 0 8*8 80 0 0 0 80 4*0 8 0
  //   8 8 0 0 0 8 0 8 8 0 0 80 80 80 6*40 42 7*40 42 7*40 42 7*40 42 7*40 42 7*40 42 7*40 42 40 8*0 8 6*0
  //   4 0 52*40 5*0 4 2 7*0 4 2 7*0 4 2 7*0 4 2 7*0 4 2 7*0 4 2 17*0 2 11*0 4 4*0 4*8 80 0 0 0 4*8 80 0 0
  //   0 80 0 0 0 4*8 80 0 0 0 8 0 8 0 0 8 0 8 0 8 0 0 8 0 80 80 80 6*40 42 7*40 42 7*40 42 7*40 42 7*40 42
  //   7*40 42 7*40 42 40 8*0 8 6*0 4 0 52*40 5*0 4 2 7*0 4 2 7*0 4 2 7*0 4 2 7*0 4 2 7*0 4 2 17*0 2 11*0 4
  //   4*0 4*8 80 0 0 0 4*8 80 0 0 0 4*8 80 0 0 0 80 0 0 0 8 0 8 0 8 0 0 8 0 8 0 8 0 0 80 80 80 6*40 42
  //   7*40 42 7*40 42 7*40 42 7*40 42 7*40 42 7*40 42 40 8*0 8 6*0 4 0 52*40 5*0 4 2 7*0 4 2 7*0 4 2 7*0 4
  //   2 7*0 4 2 7*0 4 2 17*0 2 11*0 4 4*0 4*8 80 0 0 0 80 0 0 0 4*8 80 0 0 0 4*8 80 0 0 0 8 0 0 8 0 8 0 8
  //   0 0 8 0 8 0 80 80 80 6*40 42 7*40 42 7*40 42 7*40 42 7*40 42 7*40 42 7*40 42 40 8*0 8 6*0 4 0 52*40
  //   5*0 4 2 7*0 4 2 7*0 4 2 7*0 4 2 7*0 4 2 7*0 4 2 17*0 2 11*0 4 4*0 4*8 80 0 0 0 80 0 0 0 8*8 80 0 0 0
  //   80 0 0 0 8 0 0 8 8 0 0 8 0 0 8 8 0 0 80 80 80 6*40 42 7*40 42 7*40 42 7*40 42 7*40 42 7*40 42 7*40
  //   42 40 9*0 7*8 0 52*80 54*8 9*0 7*8 0 8 0 0 0 8*8 7*0 80 0 0 0 80 11*0 80 24*0 16*4 24*5 16*4 9*0 7*8
  //   0 52*80 54*8 9*0 7*8 0 8 0 0 0 8*8 7*0 80 0 0 0 80 7*0 80 28*0 16*4 24*5 16*4 9*0 7*8 0 52*80 54*8
  //   9*0 7*8 0 8 0 0 0 8*8 7*0 80 7*0 80 7*0 80 24*0 16*4 24*5 16*4 9*0 7*8 0 52*80 54*8 9*0 7*8 0 8 0 0
  //   0 8*8 7*0 80 7*0 80 0 0 0 80 28*0 16*4 24*5 16*4 9*0 7*8 0 52*80 54*8 9*0 7*8 0 8 0 0 0 8*8 0 0 0 80
  //   7*0 80 11*0 80 24*0 16*4 24*5 16*4 9*0 7*8 0 52*80 54*8 9*0 7*8 0 8 0 0 0 8*8 0 0 0 80 7*0 80 7*0 80
  //   28*0 16*4 24*5 16*4 9*0 7*8 0 52*80 54*8 9*0 7*8 0 8 0 0 0 8*8 0 0 0 80 11*0 80 7*0 80 24*0 16*4
  //   24*5 16*4 9*0 7*8 0 52*80 54*8 9*0 7*8 0 8 0 0 0 8*8 0 0 0 80 11*0 80 0 0 0 80 28*0 16*4 24*5 16*4
  //   16*0 8 6*10 14 5*10 14 5*10 14 5*10 14 7*10 12 5*10 12 5*10 12 5*10 12 10 54*0 9*8 7*0 8 0 8 8 8 8*0
  //   8 8 8 20 8 8 8 8*0 20 8 8 8 20 8 8 8 4*0 20 8 8 8 80 0 0 80 80 0 80 8 0 0 8 8 0 8 20 20 20 56*8 16*0
  //   8 6*10 14 5*10 14 5*10 14 5*10 14 7*10 12 5*10 12 5*10 12 5*10 12 10 54*0 9*8 7*0 8 0 8 8 8 8*0 8 8
  //   8 20 8 8 8 8*0 20 8 8 8 4*0 20 8 8 8 20 8 8 8 80 0 0 80 0 80 80 8 0 0 8 0 8 8 20 20 20 56*8 16*0 8
  //   6*10 14 5*10 14 5*10 14 5*10 14 7*10 12 5*10 12 5*10 12 5*10 12 10 54*0 9*8 7*0 8 0 8 8 8 8*0 8 8 8
  //   20 8 8 8 4*0 20 8 8 8 4*0 20 8 8 8 4*0 20 8 8 8 80 0 80 0 80 0 80 8 0 8 0 8 0 8 20 20 20 56*8 16*0 8
  //   6*10 14 5*10 14 5*10 14 5*10 14 7*10 12 5*10 12 5*10 12 5*10 12 10 54*0 9*8 7*0 8 0 8 8 8 8*0 8 8 8
  //   20 8 8 8 4*0 20 8 8 8 8*0 20 8 8 8 20 8 8 8 80 0 80 0 0 80 80 8 0 8 0 0 8 8 20 20 20 56*8 16*0 8
  //   6*10 14 5*10 14 5*10 14 5*10 14 7*10 12 5*10 12 5*10 12 5*10 12 10 54*0 9*8 7*0 8 0 8 8 8 8*0 8 8 8
  //   4*0 20 8 8 8 4*0 20 8 8 8 20 8 8 8 4*0 20 8 8 8 0 80 0 80 80 0 80 0 8 0 8 8 0 8 20 20 20 56*8 16*0 8
  //   6*10 14 5*10 14 5*10 14 5*10 14 7*10 12 5*10 12 5*10 12 5*10 12 10 54*0 9*8 7*0 8 0 8 8 8 8*0 8 8 8
  //   4*0 20 8 8 8 4*0 20 8 8 8 4*0 20 8 8 8 20 8 8 8 0 80 0 80 0 80 80 0 8 0 8 0 8 8 20 20 20 56*8 16*0 8
  //   6*10 14 5*10 14 5*10 14 5*10 14 7*10 12 5*10 12 5*10 12 5*10 12 10 54*0 9*8 7*0 8 0 8 8 8 8*0 8 8 8
  //   4*0 20 8 8 8 20 8 8 8 4*0 20 8 8 8 4*0 20 8 8 8 0 80 80 0 80 0 80 0 8 8 0 8 0 8 20 20 20 56*8 16*0 8
  //   6*10 14 5*10 14 5*10 14 5*10 14 7*10 12 5*10 12 5*10 12 5*10 12 10 54*0 9*8 7*0 8 0 8 8 8 8*0 8 8 8
  //   4*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
  //   contents of rom_3 (hex, n*v repeats v):
  //   41 7*40 c0 8*40 18*20 8*40 72*20 a0 20 28 a0 20 28 a0 20 28 7*20 30 15*20 40 22 22 22 8*41 40 22 22
  //   22 40 22 22 22 4*41 40 22 22 22 30 41 41 30 30 41 30 22 41 41 22 22 41 22 10*20 40 7*20 40 7*20 40
  //   7*20 40 7*20 40 7*20 40 7*20 40 20 7*0 41 7*40 c0 8*40 18*20 8*40 72*20 a0 20 28 a0 20 28 a0 20 28
  //   7*20 30 15*20 40 22 22 22 8*41 40 22 22 22 4*41 40 22 22 22 40 22 22 22 30 41 41 30 41 30 30 22 41
  //   41 22 41 22 22 10*20 40 7*20 40 7*20 40 7*20 40 7*20 40 7*20 40 7*20 40 20 7*0 41 7*40 c0 8*40 18*20
  //   8*40 72*20 a0 20 28 a0 20 28 a0 20 28 7*20 30 15*20 40 22 22 22 4*41 40 22 22 22 4*41 40 22 22 22
  //   4*41 40 22 22 22 30 41 30 41 30 41 30 22 41 22 41 22 41 22 10*20 40 7*20 40 7*20 40 7*20 40 7*20 40
  //   7*20 40 7*20 40 20 7*0 41 7*40 c0 8*40 18*20 8*40 72*20 a0 20 28 a0 20 28 a0 20 28 7*20 30 15*20 40
  //   22 22 22 4*41 40 22 22 22 8*41 40 22 22 22 40 22 22 22 30 41 30 41 41 30 30 22 41 22 41 41 22 22
  //   10*20 40 7*20 40 7*20 40 7*20 40 7*20 40 7*20 40 7*20 40 20 7*0 41 7*40 c0 8*40 18*20 8*40 72*20 a0
  //   20 28 a0 20 28 a0 20 28 7*20 30 15*20 4*41 40 22 22 22 4*41 40 22 22 22 40 22 22 22 4*41 40 22 22 22
  //   41 30 41 30 30 41 30 41 22 41 22 22 41 22 10*20 40 7*20 40 7*20 40 7*20 40 7*20 40 7*20 40 7*20 40
  //   20 7*0 41 7*40 c0 8*40 18*20 8*40 72*20 a0 20 28 a0 20 28 a0 20 28 7*20 30 15*20 4*41 40 22 22 22
  //   4*41 40 22 22 22 4*41 40 22 22 22 40 22 22 22 41 30 41 30 41 30 30 41 22 41 22 41 22 22 10*20 40
  //   7*20 40 7*20 40 7*20 40 7*20 40 7*20 40 7*20 40 20 7*0 41 7*40 c0 8*40 18*20 8*40 72*20 a0 20 28 a0
  //   20 28 a0 20 28 7*20 30 15*20 4*41 40 22 22 22 40 22 22 22 4*41 40 22 22 22 4*41 40 22 22 22 41 30 30
  //   41 30 41 30 41 22 22 41 22 41 22 10*20 40 7*20 40 7*20 40 7*20 40 7*20 40 7*20 40 7*20 40 20 7*0 41
  //   7*40 c0 8*40 18*20 8*40 72*20 a0 20 28 a0 20 28 a0 20 28 7*20 30 15*20 4*41 40 22 22 22 40 22 22 22
  //   8*41 40 22 22 22 40 22 22 22 41 30 30 41 41 30 30 41 22 22 41 41 22 22 10*20 40 7*20 40 7*20 40 7*20
  //   40 7*20 40 7*20 40 7*20 40 20 8*0 7*41 9*40 18*20 8*40 18*20 54*41 20 20 30 20 20 30 20 20 30 7*41
  //   28 41 20 20 20 8*41 20 20 20 64 24 24 24 40 22 22 22 40 22 22 22 64 24 24 24 64 24 24 24 40 22 22 22
  //   64 24 24 24 28 30 30 28 28 30 28 24 22 22 24 24 22 24 59*20 9*0 7*41 9*40 18*20 8*40 18*20 54*41 20
  //   20 30 20 20 30 20 20 30 7*41 28 41 20 20 20 8*41 20 20 20 64 24 24 24 40 22 22 22 40 22 22 22 64 24
  //   24 24 40 22 22 22 64 24 24 24 64 24 24 24 28 30 30 28 30 28 28 24 22 22 24 22 24 24 59*20 9*0 7*41
  //   9*40 18*20 8*40 18*20 54*41 20 20 30 20 20 30 20 20 30 7*41 28 41 20 20 20 8*41 20 20 20 64 24 24 24
  //   40 22 22 22 64 24 24 24 40 22 22 22 64 24 24 24 40 22 22 22 64 24 24 24 28 30 28 30 28 30 28 24 22
  //   24 22 24 22 24 59*20 9*0 7*41 9*40 18*20 8*40 18*20 54*41 20 20 30 20 20 30 20 20 30 7*41 28 41 20
  //   20 20 8*41 20 20 20 64 24 24 24 40 22 22 22 64 24 24 24 40 22 22 22 40 22 22 22 64 24 24 24 64 24 24
  //   24 28 30 28 30 30 28 28 24 22 24 22 22 24 24 59*20 9*0 7*41 9*40 18*20 8*40 18*20 54*41 20 20 30 20
  //   20 30 20 20 30 7*41 28 41 20 20 20 8*41 20 20 20 40 22 22 22 64 24 24 24 40 22 22 22 64 24 24 24 64
  //   24 24 24 40 22 22 22 64 24 24 24 30 28 30 28 28 30 28 22 24 22 24 24 22 24 59*20 9*0 7*41 9*40 18*20
  //   8*40 18*20 54*41 20 20 30 20 20 30 20 20 30 7*41 28 41 20 20 20 8*41 20 20 20 40 22 22 22 64 24 24
  //   24 40 22 22 22 64 24 24 24 40 22 22 22 64 24 24 24 64 24 24 24 30 28 30 28 30 28 28 22 24 22 24 22
  //   24 24 59*20 9*0 7*41 9*40 18*20 8*40 18*20 54*41 20 20 30 20 20 30 20 20 30 7*41 28 41 20 20 20 8*41
  //   20 20 20 40 22 22 22 64 24 24 24 64 24 24 24 40 22 22 22 64 24 24 24 40 22 22 22 64 24 24 24 30 28
  //   28 30 28 30 28 22 24 24 22 24 22 24 59*20 9*0 7*41 9*40 18*20 8*40 18*20 54*41 20 20 30 20 20 30 20
  //   20 30 7*41 28 41 20 20 20 8*41 20 20 20 40 22 22 22 64 24 24 24 64 24 24 24 40 22 22 22 40 22 22 22
  //   64 24 24 24 64 24 24 24 30 28 28 30 30 28 28 22 24 24 22 22 24 24 59*20 16*0 41 52*20 54*0 9*41 7*0
  //   41 0 41 41 41 8*0 41 41 41 22 41 41 41 64 24 24 24 64 24 24 24 22 41 41 41 22 41 41 41 64 24 24 24
  //   22 41 41 41 40 28 28 40 40 28 40 41 24 24 41 41 24 41 20 20 20 56*41 16*0 41 52*20 54*0 9*41 7*0 41
  //   0 41 41 41 8*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
  //   contents of rom_4 (hex, n*v repeats v):
  //   116*8 a 8 8 a 8 8 a 13*8 11*0 35*8 0 8 8 0 0 8 0 60*8 7*0 116*8 a 8 8 a 8 8 a 13*8 11*0 35*8 0 8 8 0
  //   8 0 0 60*8 7*0 116*8 a 8 8 a 8 8 a 13*8 11*0 35*8 0 8 0 8 0 8 0 60*8 7*0 116*8 a 8 8 a 8 8 a 13*8
  //   11*0 35*8 0 8 0 8 8 0 0 60*8 7*0 116*8 a 8 8 a 8 8 a 13*8 11*0 36*8 0 8 0 0 8 0 60*8 7*0 116*8 a 8 8
  //   a 8 8 a 13*8 11*0 36*8 0 8 0 8 0 0 60*8 7*0 116*8 a 8 8 a 8 8 a 13*8 11*0 36*8 0 0 8 0 8 0 60*8 7*0
  //   116*8 a 8 8 a 8 8 a 13*8 11*0 36*8 0 0 8 8 0 0 60*8 8*0 7*8 9 106*8 9 c 8 9 c 8 9 c 21*8 0 0 0 35*8
  //   7*0 8 8 8 8*98 8*68 8*48 8*68 8*18 8*98 8*f8 9*0 7*8 9 106*8 9 c 8 9 c 8 9 c 21*8 0 0 0 35*8 7*0 8 8
  //   8 8*98 8*68 8*48 8*68 8*18 8*98 8*f8 9*0 7*8 9 106*8 9 c 8 9 c 8 9 c 21*8 0 0 0 35*8 7*0 8 8 8 8*98
  //   8*68 8*48 8*68 8*18 8*98 8*f8 9*0 7*8 9 106*8 9 c 8 9 c 8 9 c 21*8 0 0 0 35*8 7*0 8 8 8 8*98 8*68
  //   8*48 8*68 8*18 8*98 8*f8 9*0 7*8 9 106*8 9 c 8 9 c 8 9 c 21*8 0 0 0 35*8 7*0 8 8 8 8*98 8*68 8*48
  //   8*68 8*18 8*98 8*f8 9*0 7*8 9 106*8 9 c 8 9 c 8 9 c 21*8 0 0 0 35*8 7*0 8 8 8 8*98 8*68 8*48 8*68
  //   8*18 8*98 8*f8 9*0 7*8 9 106*8 9 c 8 9 c 8 9 c 21*8 0 0 0 35*8 7*0 8 8 8 8*98 8*68 8*48 8*68 8*18
  //   8*98 8*f8 9*0 7*8 9 106*8 9 c 8 9 c 8 9 c 21*8 0 0 0 35*8 7*0 8 8 8 8*98 8*68 8*48 8*68 8*18 8*98
  //   8*f8 16*0 53*8 54*0 9*8 7*0 8 0 8 8 8 8*0 39*8 0 0 8 8 0 60*8 16*0 53*8 54*0 9*8 7*0 8 0 8 8 8 8*0
  //   39*8 0 0 8 0 61*8 16*0 53*8 54*0 9*8 7*0 8 0 8 8 8 8*0 39*8 0 8 0 8 0 60*8 16*0 53*8 54*0 9*8 7*0 8
  //   0 8 8 8 8*0 39*8 0 8 0 0 61*8 16*0 53*8 54*0 9*8 7*0 8 0 8 8 8 8*0 38*8 0 8 0 8 8 0 60*8 16*0 53*8
  //   54*0 9*8 7*0 8 0 8 8 8 8*0 38*8 0 8 0 8 0 61*8 16*0 53*8 54*0 9*8 7*0 8 0 8 8 8 8*0 38*8 0 8 8 0 8 0
  //   60*8 16*0 53*8 54*0 9*8 7*0 8 0 8 8 8 8*0 38*8 0 8 8 0 0 61*8 17*0 52*8 86*0 8 0 0 0 9*8 0 0 0 8 0 0
  //   0 5*8 0 0 0 7*8 0 8 8 0 0 8 77*0 52*8 86*0 8 0 0 0 9*8 0 0 0 5*8 0 0 0 8 0 0 0 7*8 0 8 8 0 8 78*0
  //   52*8 86*0 8 0 0 0 5*8 0 0 0 5*8 0 0 0 5*8 0 0 0 7*8 0 8 0 8 0 8 77*0 52*8 86*0 8 0 0 0 5*8 0 0 0 9*8
  //   0 0 0 8 0 0 0 7*8 0 8 0 8 8 78*0 52*8 86*0 5*8 0 0 0 5*8 0 0 0 8 0 0 0 5*8 0 0 0 8*8 0 8 0 0 8 77*0
  //   52*8 86*0 5*8 0 0 0 5*8 0 0 0 5*8 0 0 0 8 0 0 0 8*8 0 8 0 8 78*0 52*8 86*0 5*8 0 0 0 8 0 0 0 5*8 0 0
  //   0 5*8 0 0 0 8*8 0 0 8 0 8 77*0 52*8 86*0 5*8 0 0 0 8 0 0 0 9*8 0 0 0 8 0 0 0 8*8 0 0 8 8 220*0 8 0 0
  //   0 8 11*0 8 7*0 7*8 225*0 8 0 0 0 8 7*0 8 11*0 7*8 225*0 8 7*0 8 7*0 8 7*0 7*8 225*0 8 7*0 8 0 0 0 8
  //   11*0 7*8 221*0 8 7*0 8 11*0 8 7*0 7*8 221*0 8 7*0 8 7*0 8 11*0 7*8 221*0 8 11*0 8 7*0 8 7*0 7*8
  //   221*0 8 11*0 8 0 0 0 8 11*0 7*8 249*0 7*8 249*0 7*8 249*0 7*8 249*0 7*8 249*0 7*8 249*0 7*8 249*0
  //   7*8 249*0 7*8 250*0 8 8 0 0 8 251*0 8 8 0 8 252*0 8 0 8 0 8 251*0 8 0 8 8 251*0 8 0 8 0 0 8 250*0 8
  //   0 8 0 8 251*0 8 0 0 8 0 8 250*0 8 0 0 8 8
  //   contents of rom_5 (hex, n*v repeats v):
  //   fd e1 e5 e9 ed f1 f5 10*fd 6*1d 6*5d 6*9d 8*fd 6*1d 6*5d 6*9d 5 9 d 11 15 1d e1 1d e1 21 29 2d 31 35
  //   3d e5 3d e5 41 45 4d 51 55 5d e9 5d e9 61 65 69 71 75 7d ed 7d ed 81 85 89 8d 95 9d f1 9d f1 a1 a5
  //   a9 ad b1 bd f5 bd f5 1d e1 e1 5d e9 e9 9d f1 f1 1e 3e 5e 7e 9e be fe fe fe 3e 7e be e3 e7 eb ef f3
  //   f7 ff ff e3 eb f3 fd 1d 5d 9d 9*fd 1d 5d 9d fd 1d 5d 9d 5*fd 1d 5d 9d fe fd fd fe fe fd fe ff fd fd
  //   ff ff fd ff 1d 5d 9d 1d 3d 5d 7d 9d bd fd fd 1d 3d 5d 7d 9d bd fd fd 1d 3d 5d 7d 9d bd fd fd 1d 3d
  //   5d 7d 9d bd fd fd 1d 3d 5d 7d 9d bd fd fd 1d 3d 5d 7d 9d bd fd fd 1d 3d 5d 7d 9d bd fd fd fd 7*0 fd
  //   e1 e5 e9 ed f1 f5 10*fd 6*1d 6*5d 6*9d 8*fd 6*1d 6*5d 6*9d 5 9 d 11 15 1d e1 1d e1 21 29 2d 31 35 3d
  //   e5 3d e5 41 45 4d 51 55 5d e9 5d e9 61 65 69 71 75 7d ed 7d ed 81 85 89 8d 95 9d f1 9d f1 a1 a5 a9
  //   ad b1 bd f5 bd f5 1d e1 e1 5d e9 e9 9d f1 f1 1e 3e 5e 7e 9e be fe fe fe 3e 7e be e3 e7 eb ef f3 f7
  //   ff ff e3 eb f3 fd 1d 5d 9d 9*fd 1d 5d 9d 5*fd 1d 5d 9d fd 1d 5d 9d fe fd fd fe fd fe fe ff fd fd ff
  //   fd ff ff 1d 5d 9d 1d 3d 5d 7d 9d bd fd fd 1d 3d 5d 7d 9d bd fd fd 1d 3d 5d 7d 9d bd fd fd 1d 3d 5d
  //   7d 9d bd fd fd 1d 3d 5d 7d 9d bd fd fd 1d 3d 5d 7d 9d bd fd fd 1d 3d 5d 7d 9d bd fd fd fd 7*0 fd e1
  //   e5 e9 ed f1 f5 10*fd 6*1d 6*5d 6*9d 8*fd 6*1d 6*5d 6*9d 5 9 d 11 15 1d e1 1d e1 21 29 2d 31 35 3d e5
  //   3d e5 41 45 4d 51 55 5d e9 5d e9 61 65 69 71 75 7d ed 7d ed 81 85 89 8d 95 9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
endmodule

module StepCounter (
  input  Clk,
  input  NotReset,
  input  Clear,
  input  NotHalt,
  input  NotWait,
  output [3:0] Step
);

  wire and_1_out, n74161_1_pin3, n74161_1_pin4, n74161_1_pin5, n74161_1_pin6, n74161_1_pin10, not_1_out;

  not not_1 (not_1_out, Clear);
  and and_1 (and_1_out, NotHalt, NotWait);
  _74161 u_74161_1 (
    .pin1(NotReset), .pin2(Clk), .pin3(n74161_1_pin3), .pin4(n74161_1_pin4), .pin5(n74161_1_pin5),
    .pin6(n74161_1_pin6), .pin7(and_1_out), .pin14(Step[0]), .pin13(Step[1]), .pin12(Step[2]),
    .pin11(Step[3]), .pin10(n74161_1_pin10), .pin9(not_1_out));  // open: pin15
  // also tied to GND on the sheet: {n74161_1_pin3, n74161_1_pin4, n74161_1_pin5, n74161_1_pin6}
  // also tied to VCC on the sheet: n74161_1_pin10
endmodule

module ProgramCounter (
  input  NotReset,
  input  DHWrite,
  input  Clk,
  input  DHRead,
  input  [7:0] DIn,
  input  ARead,
  input  DLWrite,
  input  NotInc,
  input  DLRead,
  output [7:0] DOut,
  output [15:0] AOut
);

  wire counter_2_carry, not_1_out, not_2_out;
  wire [3:0] counter_1_q, counter_1_q_2, counter_2_q, counter_2_q_2;

  not not_1 (not_1_out, NotReset);
  not not_2 (not_2_out, NotInc);
  Counter counter_1 (
    .clr(not_1_out), .load(DHWrite), .up(counter_2_carry), .count(counter_2_carry), .clk(Clk), .D(DIn),
    .Q({counter_1_q_2, counter_1_q}));  // open: carry
  Counter counter_2 (
    .clr(not_1_out), .load(DLWrite), .up(not_2_out), .count(not_2_out), .clk(Clk), .D(DIn),
    .carry(counter_2_carry), .Q({counter_2_q_2, counter_2_q}));
  assign DOut = DHRead ? {counter_1_q_2, counter_1_q} : 8'bz;  // Controlled_Buffer controlled_buffer_1
  assign AOut = ARead ? {counter_1_q_2, counter_1_q, counter_2_q_2, counter_2_q} : 16'bz;  // Controlled_Buffer controlled_buffer_2
  assign DOut = DLRead ? {counter_2_q_2, counter_2_q} : 8'bz;  // Controlled_Buffer controlled_buffer_3
  Hex_Digit_Display hex_digit_display_1 (.value(counter_1_q_2));  // open: dp
  Hex_Digit_Display hex_digit_display_2 (.value(counter_1_q));  // open: dp
  Hex_Digit_Display hex_digit_display_3 (.value(counter_2_q_2));  // open: dp
  Hex_Digit_Display hex_digit_display_4 (.value(counter_2_q));  // open: dp
endmodule
